# Fritzing sketch Elanus (saved by Fritzing 0.9.3b)

parts:
  Raspberry_Pi_1 = Raspberry Pi 3 [part_number=RPI-3-V1.2]
  GY2 = MPU-6050 Board GY-521 [form="♀ (female)" package=THT]
  S2 = H-Bridge with L298N
  M1 = DC Motor
  M2 = DC Motor
  M3 = DC Motor
  M4 = DC Motor
  VCC1 = 4 x AAA Battery Mount

nets:
  N1: Raspberry_Pi_1.3v3, GY2.pin1
  N2: Raspberry_Pi_1.GPIO2, GY2.pin4
  N3: Raspberry_Pi_1.GPIO3, GY2.pin3
  GND: Raspberry_Pi_1.GND, GY2.pin2, S2.GND, VCC1.-
  N4: Raspberry_Pi_1.GIPO17, S2.IN1
  N5: Raspberry_Pi_1.GIPO22, S2.IN2
  N6: Raspberry_Pi_1.GIPO24, S2.IN4
  N7: Raspberry_Pi_1.GIPO23, S2.IN3
  N8: S2.12V, VCC1.+
  N9: S2.M1-01, M1.pin_2, M2.pin_2
  N10: S2.M1-02, M1.pin_1, M2.pin_1
  N11: S2.M2-01, M3.pin_1, M4.pin_1
  N12: S2.M2-02, M3.pin_2, M4.pin_2

custom parts:
  MPU-6050 Board GY-521: Acelerometro y Giroscopio MPU-6050 Board GY-521
  H-Bridge with L298N: h-bridge
